# Fritzing sketch test03LED_Blink (saved by Fritzing 0.9.3b)
breadboards: 1

parts:
  R1 = Resistor [tolerance=±5% resistance=220 package=THT]
  LED1 = LED - 5mm [color="Red (633nm)" package="5 mm [THT]"]
  부품1 = Arduino Uno (Rev3)

nets:
  N1: R1.Pin_0, LED1.anode
  N2: R1.Pin_1, 부품1.D2
  N3: LED1.cathode, 부품1.GND
