# Fritzing sketch test03LED_Blinks (saved by Fritzing 0.9.3b)
breadboards: 1

parts:
  LED1 = LED - 5mm [color="Red (633nm)" package="5 mm [THT]"]
  부품1 = Arduino Uno (Rev3)
  R1 = Resistor [tolerance=±5% resistance=220 package=THT]
  R2 = Resistor [tolerance=±5% resistance=220 package=THT]
  LED2 = LED - 5mm [color="Red (633nm)" package="5 mm [THT]"]
  LED3 = LED - 5mm [color="Red (633nm)" package="5 mm [THT]"]
  LED4 = LED - 5mm [color="Red (633nm)" package="5 mm [THT]"]
  LED5 = LED - 5mm [color="Red (633nm)" package="5 mm [THT]"]
  R3 = Resistor [tolerance=±5% resistance=220 package=THT]
  R4 = Resistor [tolerance=±5% resistance=220 package=THT]
  R5 = Resistor [tolerance=±5% resistance=220 package=THT]

nets:
  N1: LED1.cathode, 부품1.GND, LED2.cathode, LED3.cathode, LED4.cathode, LED5.cathode
  N2: LED1.anode, R1.Pin_1
  N3: 부품1.D2, R5.Pin_0
  N4: 부품1.D3_PWM, R4.Pin_0
  N5: 부품1.D4, R3.Pin_0
  N6: 부품1.D5_PWM, R2.Pin_0
  N7: 부품1.D6_PWM, R1.Pin_0
  N8: R2.Pin_1, LED2.anode
  N9: LED3.anode, R3.Pin_1
  N10: LED4.anode, R4.Pin_1
  N11: LED5.anode, R5.Pin_1
