# Fritzing sketch test05RGB_LED (saved by Fritzing 0.9.3b)
breadboards: 1

parts:
  부품1 = Arduino Uno (Rev3)
  LED1 = RGB LED (com. cathode, rgb) [package="5 mm [THT]"]

nets:
  N1: 부품1.D10_PWM/SS, LED1.common_cathode
  N2: 부품1.GND, LED1.blue_anode
