# Fritzing sketch test07LED_Button (saved by Fritzing 0.9.3b)
breadboards: 1

parts:
  R1 = Resistor [tolerance=±5% resistance=220 package=THT]
  LED1 = LED - 5mm [color="Red (633nm)" package="5 mm [THT]"]
  부품1 = Arduino Uno (Rev3)
  S1 = Pushbutton [package="[THT]"]
  R2 = Resistor [tolerance=±5% resistance=220 package=THT]

nets:
  N1: R1.Pin_0, LED1.anode
  N2: R1.Pin_1, 부품1.D2
  N3: LED1.cathode, 부품1.GND, R2.Pin_1
  N4: 부품1.D7, S1.Pin_1, S1.Pin_2, R2.Pin_0
  N5: 부품1.5V, S1.Pin_3, S1.Pin_4
