# Fritzing sketch test09analogRead (saved by Fritzing 0.9.3b)
breadboards: 1

parts:
  부품1 = Arduino Uno (Rev3)
  RE1 = Rotary Encoder [package=THT]
  LED1 = LED - 5mm [color="Red (633nm)" package="5 mm [THT]"]
  R1 = Resistor [tolerance=±5% resistance=220 package=THT]

nets:
  N1: 부품1.A0, RE1.EncoderPinC
  N2: 부품1.D3_PWM, R1.Pin_1
  N3: 부품1.GND, LED1.cathode
  N4: LED1.anode, R1.Pin_0
