# Fritzing sketch test10Servo2 (saved by Fritzing 0.9.3b)
breadboards: 1

parts:
  부품2 = Arduino Uno (Rev3)
  J1 = Basic Servo
  J2 = Basic Servo

nets:
  N1: 부품2.D8, J2.pulse
  N2: 부품2.D7, J1.pulse
  VCC: 부품2.5V, J1.vcc, J2.vcc
  GND: 부품2.GND, J1.gnd, J2.gnd
