# Fritzing sketch test22LineTrackingSensor (saved by Fritzing 0.9.3b)
breadboards: 1

parts:
  부품1 = Arduino Uno (Rev3)
  부품3 = Max Power IR LED Kit

nets:
  N1: 부품1.D2, 부품3.VCC
  N2: 부품1.5V, 부품3.CONTROL
  GND: 부품1.GND, 부품3.GND
