# Fritzing sketch test23LaserOUTPUT (saved by Fritzing 0.9.3b)
breadboards: 1

parts:
  부품1 = Arduino Uno (Rev3)
  부품2 = Humidity Sensor - HIH-4030 Breakout

nets:
  N1: 부품1.D2, 부품2.OUT
  GND: 부품1.GND, 부품2.GND
