# Fritzing sketch test24RelayController (saved by Fritzing 0.9.3b)
breadboards: 1

parts:
  부품1 = Arduino Uno (Rev3)
  U2 = G3VM-61E1 [package=g3vm-61e1]
  LED1 = LED - 5mm [color="Red (633nm)" package="5 mm [THT]"]
  R1 = Resistor [tolerance=±5% resistance=220 package=THT]
  VCC1 = Battery

nets:
  N1: 부품1.D2, U2.P$4
  N2: 부품1.5V, U2.P$5
  N3: 부품1.GND, U2.P$6
  N4: U2.P$2, R1.Pin_1
  N5: LED1.cathode, VCC1.-
  N6: LED1.anode, R1.Pin_0
