# Fritzing sketch test26DotMatrix8_8 (saved by Fritzing 0.9.3b)
breadboards: 1

parts:
  부품1 = Arduino Uno (Rev3)
  Disp1 = LBT2088AH [part_number=LBT2088AH]
  R1 = Resistor [tolerance=±5% resistance=220 package=THT]

nets:
  N1: 부품1.D2, Disp1.pin_9
  N2: 부품1.D3_PWM, R1.Pin_0
  N3: Disp1.pin_3, Disp1.pin_4, Disp1.pin_6, Disp1.pin_10, Disp1.pin_11, Disp1.pin_13, Disp1.pin_15, Disp1.pin_16, R1.Pin_1
